// Logisim project ProyectoMIPS.circ as structural Verilog: 9 circuits, main circuit main
// address
module main (
  input  Active_Load,
  input  Active_Store,
  input  Reset,
  input  [31:0] in_4,
  output [31:0] out_5
);

  wire clock, letter_1_out_2, letter_1_out_3, letter_1_out_4, letter_1_out_5, letter_1_out_6, letter_1_out_7,
       letter_1_out_8, letter_2_out_2, letter_2_out_3, letter_2_out_4, letter_2_out_5, letter_2_out_6,
       letter_2_out_7, letter_2_out_8, letter_3_out_2, letter_3_out_3, letter_3_out_4, letter_3_out_5,
       letter_3_out_6, letter_3_out_7, letter_3_out_8, num_1_out_2, num_1_out_3, num_1_out_4, num_1_out_5,
       num_1_out_6, num_1_out_7, num_1_out_8, num_2_out_2, num_2_out_3, num_2_out_4, num_2_out_5,
       num_2_out_6, num_2_out_7, num_2_out_8, num_3_out_2, num_3_out_3, num_3_out_4, num_3_out_5,
       num_3_out_6, num_3_out_7, num_3_out_8, num_4_out_2, num_4_out_3, num_4_out_4, num_4_out_5,
       num_4_out_6, num_4_out_7, num_4_out_8, num_5_out_2, num_5_out_3, num_5_out_4, num_5_out_5,
       num_5_out_6, num_5_out_7, num_5_out_8, num_6_out_2, num_6_out_3, num_6_out_4, num_6_out_5,
       num_6_out_6, num_6_out_7, num_6_out_8, num_7_out_2, num_7_out_3, num_7_out_4, num_7_out_5,
       num_7_out_6, num_7_out_7, num_7_out_8, num_8_out_2, num_8_out_3, num_8_out_4, num_8_out_5,
       num_8_out_6, num_8_out_7, num_8_out_8, num_9_out_2, num_9_out_3, num_9_out_4, num_9_out_5,
       num_9_out_6, num_9_out_7, num_9_out_8, num_10_out_2, num_10_out_3, num_10_out_4, num_10_out_5,
       num_10_out_6, num_10_out_7, num_10_out_8, num_11_out_2, num_11_out_3, num_11_out_4, num_11_out_5,
       num_11_out_6, num_11_out_7, num_11_out_8, num_12_out_2, num_12_out_3, num_12_out_4, num_12_out_5,
       num_12_out_6, num_12_out_7, num_12_out_8, num_13_out_2, num_13_out_3, num_13_out_4, num_13_out_5,
       num_13_out_6, num_13_out_7, num_13_out_8, num_14_out_2, num_14_out_3, num_14_out_4, num_14_out_5,
       num_14_out_6, num_14_out_7, num_14_out_8, num_15_out_2, num_15_out_3, num_15_out_4, num_15_out_5,
       num_15_out_6, num_15_out_7, num_15_out_8, rd0, rd1, rd2, rd3, rd4, Reset_out, rs0, rs1, rs2, rs3, rs4,
       rt0, rt1, rt2, rt3, rt4;
  wire [3:0] bit_extender_1_out;
  wire [4:0] decode_1_rd, decode_1_rs, decode_1_rt;
  wire [5:0] decode_1_funct_op;
  wire [6:0] s1, s2, s3;
  wire [15:0] address;
  wire [23:0] adder_1_out, register_1_q;
  wire [25:0] addressJ;

  Register_part #(.width(24)) register_1 (.D(adder_1_out), .Q(register_1_q), .clk(clock), .clr(Reset_out));  // open: en
  Button u_Reset (.out(Reset_out));
  Adder #(.width(24)) adder_1 (.a(register_1_q), .b(24'h1), .out(adder_1_out));  // open: cin, cout
  Clock clock_1 (.out(clock));
  RAM #(.addrWidth(24), .dataWidth(32), .bus("separate")) ram_1 (
    .addr(register_1_q), .din(in_4), .data(out_5), .str(Active_Store), .clk(clock), .ld(Active_Load),
    .clr(Reset));  // open: sel
  Decode decode_1 (
    .in_1(out_5), .Address_J(addressJ), .Address(address), .rs(decode_1_rs), .rt(decode_1_rt),
    .rd(decode_1_rd), .Funct_op(decode_1_funct_op));  // open: Shamt
  ShowOp_funct showop_funct_1 (.Funct_0p(decode_1_funct_op), .s1(s1), .s2(s2), .s2_2(s3));
  Penilla penilla_1 (.Input(decode_1_rs), .s0(rs0), .s1(rs1), .s2(rs2), .s3(rs3), .s4(rs4));
  Penilla penilla_2 (.Input(decode_1_rt), .s0(rt0), .s1(rt1), .s2(rt2), .s3(rt3), .s4(rt4));
  Penilla penilla_3 (.Input(decode_1_rd), .s0(rd0), .s1(rd1), .s2(rd2), .s3(rd3), .s4(rd4));
  _7_Segment_Display u_7_segment_display_1 (
    .g(letter_1_out_5), .f(letter_1_out_4), .a(letter_1_out_3), .b(letter_1_out_2), .e(letter_1_out_8),
    .d(letter_1_out_7), .c(letter_1_out_6));  // open: dp
  Letter letter_1 (
    .Number(s1), .out_8(letter_1_out_8), .out_7(letter_1_out_7), .out_6(letter_1_out_6),
    .out_5(letter_1_out_5), .out_4(letter_1_out_4), .out_3(letter_1_out_3), .out_2(letter_1_out_2));
  _7_Segment_Display u_7_segment_display_2 (
    .g(num_1_out_5), .f(num_1_out_4), .a(num_1_out_3), .b(num_1_out_2), .e(num_1_out_8), .d(num_1_out_7),
    .c(num_1_out_6));  // open: dp
  num num_1 (
    .in_1(rs0), .out_8(num_1_out_8), .out_7(num_1_out_7), .out_6(num_1_out_6), .out_5(num_1_out_5),
    .out_4(num_1_out_4), .out_3(num_1_out_3), .out_2(num_1_out_2));
  _7_Segment_Display u_7_segment_display_3 (
    .g(num_2_out_5), .f(num_2_out_4), .a(num_2_out_3), .b(num_2_out_2), .e(num_2_out_8), .d(num_2_out_7),
    .c(num_2_out_6));  // open: dp
  num num_2 (
    .in_1(rt0), .out_8(num_2_out_8), .out_7(num_2_out_7), .out_6(num_2_out_6), .out_5(num_2_out_5),
    .out_4(num_2_out_4), .out_3(num_2_out_3), .out_2(num_2_out_2));
  _7_Segment_Display u_7_segment_display_4 (
    .g(num_3_out_5), .f(num_3_out_4), .a(num_3_out_3), .b(num_3_out_2), .e(num_3_out_8), .d(num_3_out_7),
    .c(num_3_out_6));  // open: dp
  num num_3 (
    .in_1(rd0), .out_8(num_3_out_8), .out_7(num_3_out_7), .out_6(num_3_out_6), .out_5(num_3_out_5),
    .out_4(num_3_out_4), .out_3(num_3_out_3), .out_2(num_3_out_2));
  _7_Segment_Display u_7_segment_display_5 (
    .g(letter_2_out_5), .f(letter_2_out_4), .a(letter_2_out_3), .b(letter_2_out_2), .e(letter_2_out_8),
    .d(letter_2_out_7), .c(letter_2_out_6));  // open: dp
  Letter letter_2 (
    .Number(s2), .out_8(letter_2_out_8), .out_7(letter_2_out_7), .out_6(letter_2_out_6),
    .out_5(letter_2_out_5), .out_4(letter_2_out_4), .out_3(letter_2_out_3), .out_2(letter_2_out_2));
  _7_Segment_Display u_7_segment_display_6 (
    .g(num_4_out_5), .f(num_4_out_4), .a(num_4_out_3), .b(num_4_out_2), .e(num_4_out_8), .d(num_4_out_7),
    .c(num_4_out_6));  // open: dp
  num num_4 (
    .in_1(rs1), .out_8(num_4_out_8), .out_7(num_4_out_7), .out_6(num_4_out_6), .out_5(num_4_out_5),
    .out_4(num_4_out_4), .out_3(num_4_out_3), .out_2(num_4_out_2));
  _7_Segment_Display u_7_segment_display_7 (
    .g(num_5_out_5), .f(num_5_out_4), .a(num_5_out_3), .b(num_5_out_2), .e(num_5_out_8), .d(num_5_out_7),
    .c(num_5_out_6));  // open: dp
  num num_5 (
    .in_1(rt1), .out_8(num_5_out_8), .out_7(num_5_out_7), .out_6(num_5_out_6), .out_5(num_5_out_5),
    .out_4(num_5_out_4), .out_3(num_5_out_3), .out_2(num_5_out_2));
  _7_Segment_Display u_7_segment_display_8 (
    .g(num_6_out_5), .f(num_6_out_4), .a(num_6_out_3), .b(num_6_out_2), .e(num_6_out_8), .d(num_6_out_7),
    .c(num_6_out_6));  // open: dp
  num num_6 (
    .in_1(rd1), .out_8(num_6_out_8), .out_7(num_6_out_7), .out_6(num_6_out_6), .out_5(num_6_out_5),
    .out_4(num_6_out_4), .out_3(num_6_out_3), .out_2(num_6_out_2));
  _7_Segment_Display u_7_segment_display_9 (
    .g(letter_3_out_5), .f(letter_3_out_4), .a(letter_3_out_3), .b(letter_3_out_2), .e(letter_3_out_8),
    .d(letter_3_out_7), .c(letter_3_out_6));  // open: dp
  Letter letter_3 (
    .Number(s3), .out_8(letter_3_out_8), .out_7(letter_3_out_7), .out_6(letter_3_out_6),
    .out_5(letter_3_out_5), .out_4(letter_3_out_4), .out_3(letter_3_out_3), .out_2(letter_3_out_2));
  _7_Segment_Display u_7_segment_display_10 (
    .g(num_7_out_5), .f(num_7_out_4), .a(num_7_out_3), .b(num_7_out_2), .e(num_7_out_8), .d(num_7_out_7),
    .c(num_7_out_6));  // open: dp
  num num_7 (
    .in_1(rs2), .out_8(num_7_out_8), .out_7(num_7_out_7), .out_6(num_7_out_6), .out_5(num_7_out_5),
    .out_4(num_7_out_4), .out_3(num_7_out_3), .out_2(num_7_out_2));
  _7_Segment_Display u_7_segment_display_11 (
    .g(num_8_out_5), .f(num_8_out_4), .a(num_8_out_3), .b(num_8_out_2), .e(num_8_out_8), .d(num_8_out_7),
    .c(num_8_out_6));  // open: dp
  num num_8 (
    .in_1(rt2), .out_8(num_8_out_8), .out_7(num_8_out_7), .out_6(num_8_out_6), .out_5(num_8_out_5),
    .out_4(num_8_out_4), .out_3(num_8_out_3), .out_2(num_8_out_2));
  _7_Segment_Display u_7_segment_display_12 (
    .g(num_9_out_5), .f(num_9_out_4), .a(num_9_out_3), .b(num_9_out_2), .e(num_9_out_8), .d(num_9_out_7),
    .c(num_9_out_6));  // open: dp
  num num_9 (
    .in_1(rd2), .out_8(num_9_out_8), .out_7(num_9_out_7), .out_6(num_9_out_6), .out_5(num_9_out_5),
    .out_4(num_9_out_4), .out_3(num_9_out_3), .out_2(num_9_out_2));
  _7_Segment_Display u_7_segment_display_13 (
    .g(num_10_out_5), .f(num_10_out_4), .a(num_10_out_3), .b(num_10_out_2), .e(num_10_out_8),
    .d(num_10_out_7), .c(num_10_out_6));  // open: dp
  num num_10 (
    .in_1(rs3), .out_8(num_10_out_8), .out_7(num_10_out_7), .out_6(num_10_out_6), .out_5(num_10_out_5),
    .out_4(num_10_out_4), .out_3(num_10_out_3), .out_2(num_10_out_2));
  _7_Segment_Display u_7_segment_display_14 (
    .g(num_11_out_5), .f(num_11_out_4), .a(num_11_out_3), .b(num_11_out_2), .e(num_11_out_8),
    .d(num_11_out_7), .c(num_11_out_6));  // open: dp
  num num_11 (
    .in_1(rt3), .out_8(num_11_out_8), .out_7(num_11_out_7), .out_6(num_11_out_6), .out_5(num_11_out_5),
    .out_4(num_11_out_4), .out_3(num_11_out_3), .out_2(num_11_out_2));
  _7_Segment_Display u_7_segment_display_15 (
    .g(num_12_out_5), .f(num_12_out_4), .a(num_12_out_3), .b(num_12_out_2), .e(num_12_out_8),
    .d(num_12_out_7), .c(num_12_out_6));  // open: dp
  num num_12 (
    .in_1(rd3), .out_8(num_12_out_8), .out_7(num_12_out_7), .out_6(num_12_out_6), .out_5(num_12_out_5),
    .out_4(num_12_out_4), .out_3(num_12_out_3), .out_2(num_12_out_2));
  _7_Segment_Display u_7_segment_display_16 (
    .g(num_13_out_5), .f(num_13_out_4), .a(num_13_out_3), .b(num_13_out_2), .e(num_13_out_8),
    .d(num_13_out_7), .c(num_13_out_6));  // open: dp
  num num_13 (
    .in_1(rs4), .out_8(num_13_out_8), .out_7(num_13_out_7), .out_6(num_13_out_6), .out_5(num_13_out_5),
    .out_4(num_13_out_4), .out_3(num_13_out_3), .out_2(num_13_out_2));
  _7_Segment_Display u_7_segment_display_17 (
    .g(num_14_out_5), .f(num_14_out_4), .a(num_14_out_3), .b(num_14_out_2), .e(num_14_out_8),
    .d(num_14_out_7), .c(num_14_out_6));  // open: dp
  num num_14 (
    .in_1(rt4), .out_8(num_14_out_8), .out_7(num_14_out_7), .out_6(num_14_out_6), .out_5(num_14_out_5),
    .out_4(num_14_out_4), .out_3(num_14_out_3), .out_2(num_14_out_2));
  _7_Segment_Display u_7_segment_display_18 (
    .g(num_15_out_5), .f(num_15_out_4), .a(num_15_out_3), .b(num_15_out_2), .e(num_15_out_8),
    .d(num_15_out_7), .c(num_15_out_6));  // open: dp
  num num_15 (
    .in_1(rd4), .out_8(num_15_out_8), .out_7(num_15_out_7), .out_6(num_15_out_6), .out_5(num_15_out_5),
    .out_4(num_15_out_4), .out_3(num_15_out_3), .out_2(num_15_out_2));
  Hex_Digit_Display hex_digit_display_1 (.value(bit_extender_1_out));  // open: dp
  assign bit_extender_1_out = {{2{1'b0}}, addressJ[25:24]};  // Bit_Extender bit_extender_1
  Hex_Digit_Display hex_digit_display_2 (.value(addressJ[23:20]));  // open: dp
  Hex_Digit_Display hex_digit_display_3 (.value(addressJ[19:16]));  // open: dp
  Hex_Digit_Display hex_digit_display_4 (.value(address[11:8]));  // open: dp
  Hex_Digit_Display hex_digit_display_5 (.value(address[15:12]));  // open: dp
  Hex_Digit_Display hex_digit_display_6 (.value(addressJ[11:8]));  // open: dp
  Hex_Digit_Display hex_digit_display_7 (.value(addressJ[15:12]));  // open: dp
  Hex_Digit_Display hex_digit_display_8 (.value(address[3:0]));  // open: dp
  Hex_Digit_Display hex_digit_display_9 (.value(address[7:4]));  // open: dp
  Hex_Digit_Display hex_digit_display_10 (.value(addressJ[7:4]));  // open: dp
  Hex_Digit_Display hex_digit_display_11 (.value(addressJ[3:0]));  // open: dp

  // Notes on the sheet:
  //   FETCH
  //   RS
  //   RT
  //   Operacion
  //   RD
  //   AddressJump:
  //   Address:
endmodule

module PC (
  input  Clock,
  input  Reset,
  output [23:0] Address
);

  wire [23:0] adder_1_out;

  Adder #(.width(24)) adder_1 (.a(Address), .b(24'h1), .out(adder_1_out));  // open: cin, cout
  Register_part #(.width(24)) register_1 (.D(adder_1_out), .Q(Address), .clk(Clock), .clr(Reset));  // open: en
endmodule

module Decode (
  input  [31:0] in_1,
  output [25:0] Address_J,
  output [15:0] Address,
  output [4:0] rs,
  output [4:0] rt,
  output [4:0] rd,
  output [4:0] Shamt,
  output [5:0] Funct_op
);

  wire not_1_out;
  wire [1:0] comparator_2_eq;
  wire [25:0] demultiplexer_1_out0, demultiplexer_1_out1;

  Comparator #(.width(6)) comparator_1 (.a(in_1[31:26]), .b({6{1'b0}}), .eq(comparator_2_eq[1]));  // open: gt, lt
  Demultiplexer #(.width(26), .enable("false")) demultiplexer_1 (
    .out0(demultiplexer_1_out0), .out1({demultiplexer_1_out1[25:16], rd, Shamt, demultiplexer_1_out1[5:0]}),
    .in(in_1[25:0]), .sel(comparator_2_eq[1]));
  Comparator #(.width(6)) comparator_2 (.a(in_1[31:26]), .b(6'b000010), .eq(comparator_2_eq[0]));  // open: gt, lt
  Multiplexer #(.width(6), .enable("false")) multiplexer_1 (
    .in0(demultiplexer_1_out1[5:0]), .in1(in_1[31:26]), .out(Funct_op), .sel(not_1_out));
  not not_1 (not_1_out, comparator_2_eq[1]);
  Multiplexer #(.width(16), .enable("false")) multiplexer_2 (
    .in0(demultiplexer_1_out0[15:0]), .in1({16{1'b0}}), .out(Address), .sel(comparator_2_eq[0]));
  Multiplexer #(.width(26), .enable("false")) multiplexer_3 (
    .in0({26{1'b0}}), .in1(demultiplexer_1_out0), .out(Address_J), .sel(comparator_2_eq[0]));
  Multiplexer #(.select(2), .width(10), .enable("false")) multiplexer_4 (
    .in0(demultiplexer_1_out0[25:16]), .in1({10{1'b0}}), .in2(demultiplexer_1_out1[25:16]), .out({rs, rt}),
    .sel(comparator_2_eq));  // open: in3
endmodule

module Penilla (
  input  [4:0] Input,
  output s0,
  output s1,
  output s2,
  output s3,
  output s4
);


  assign s0 = Input[0];
  assign s1 = Input[1];
  assign s2 = Input[2];
  assign s3 = Input[3];
  assign s4 = Input[4];
endmodule

module num (
  input  in_1,
  output out_2,
  output out_3,
  output out_4,
  output out_5,
  output out_6,
  output out_7,
  output out_8
);

  Multiplexer #(.width(7), .enable("false")) multiplexer_1 (
    .in0(7'b1110111), .in1(7'b0010001), .out({out_8, out_7, out_6, out_5, out_4, out_3, out_2}), .sel(in_1));
endmodule

module ShowOp_funct (
  input  [5:0] Funct_0p,
  output [6:0] s1,
  output [6:0] s2,
  output [6:0] s2_2
);

  wire comparator_1_eq, comparator_2_eq, comparator_3_eq, comparator_4_eq, comparator_5_eq, comparator_6_eq,
       comparator_7_eq, comparator_8_eq, comparator_9_eq, comparator_10_eq, letter_1_out_2, letter_1_out_3,
       letter_1_out_4, letter_1_out_5, letter_1_out_6, letter_1_out_7, letter_1_out_8, letter_2_out_2,
       letter_2_out_3, letter_2_out_4, letter_2_out_5, letter_2_out_6, letter_2_out_7, letter_2_out_8,
       letter_3_out_2, letter_3_out_3, letter_3_out_4, letter_3_out_5, letter_3_out_6, letter_3_out_7,
       letter_3_out_8;
  wire [3:0] opchooser_1_s0;

  Comparator #(.width(6)) comparator_1 (.a(Funct_0p), .b(6'b100000), .eq(comparator_1_eq));  // open: gt, lt
  Comparator #(.width(6)) comparator_2 (.a(Funct_0p), .b(6'b100010), .eq(comparator_2_eq));  // open: gt, lt
  Comparator #(.width(6)) comparator_3 (.a(Funct_0p), .b(6'b100100), .eq(comparator_3_eq));  // open: gt, lt
  Comparator #(.width(6)) comparator_4 (.a(Funct_0p), .b(6'b100101), .eq(comparator_4_eq));  // open: gt, lt
  Comparator #(.width(6)) comparator_5 (.a(Funct_0p), .b(6'b011000), .eq(comparator_5_eq));  // open: gt, lt
  Comparator #(.width(6)) comparator_6 (.a(Funct_0p), .b(6'b000100), .eq(comparator_6_eq));  // open: gt, lt
  Comparator #(.width(6)) comparator_7 (.a(Funct_0p), .b(6'b000010), .eq(comparator_7_eq));  // open: gt, lt
  Comparator #(.width(6)) comparator_8 (.a(Funct_0p), .b(6'b100011), .eq(comparator_8_eq));  // open: gt, lt
  Comparator #(.width(6)) comparator_9 (.a(Funct_0p), .b(6'b110011), .eq(comparator_9_eq));  // open: gt, lt
  Comparator #(.width(6)) comparator_10 (.a(Funct_0p), .b(6'b001000), .eq(comparator_10_eq));  // open: gt, lt
  OpChooser opchooser_1 (
    .add(comparator_1_eq), .sub(comparator_2_eq), .\and (comparator_3_eq), .\or (comparator_4_eq),
    .mult(comparator_5_eq), .beq(comparator_6_eq), .jump(comparator_7_eq), .load(comparator_8_eq),
    .store(comparator_9_eq), .addi(comparator_10_eq), .s3(opchooser_1_s0[3]), .s2(opchooser_1_s0[2]),
    .s1(opchooser_1_s0[1]), .s0(opchooser_1_s0[0]));
  Multiplexer #(.select(4), .width(21), .enable("false")) multiplexer_1 (
    .in0(21'h20408), .in1(21'h1e7cdf), .in2(21'h1f3abe), .in3(21'h1e6bdf), .in4(21'h133b88),
    .in5(21'h113ad7), .in6(21'h7f7fc), .in7(21'h15faf1), .in8(21'h1d7ae4), .in9(21'h1d7abe),
    .in10(21'h113cdf), .out({s2_2, s2, s1}), .sel(opchooser_1_s0));  // open: in11, in12, in13, in14, in15
  _7_Segment_Display u_7_segment_display_1 (
    .g(letter_1_out_5), .f(letter_1_out_4), .a(letter_1_out_3), .b(letter_1_out_2), .e(letter_1_out_8),
    .d(letter_1_out_7), .c(letter_1_out_6));  // open: dp
  Letter letter_1 (
    .Number(s1), .out_8(letter_1_out_8), .out_7(letter_1_out_7), .out_6(letter_1_out_6),
    .out_5(letter_1_out_5), .out_4(letter_1_out_4), .out_3(letter_1_out_3), .out_2(letter_1_out_2));
  _7_Segment_Display u_7_segment_display_2 (
    .g(letter_2_out_5), .f(letter_2_out_4), .a(letter_2_out_3), .b(letter_2_out_2), .e(letter_2_out_8),
    .d(letter_2_out_7), .c(letter_2_out_6));  // open: dp
  Letter letter_2 (
    .Number(s2), .out_8(letter_2_out_8), .out_7(letter_2_out_7), .out_6(letter_2_out_6),
    .out_5(letter_2_out_5), .out_4(letter_2_out_4), .out_3(letter_2_out_3), .out_2(letter_2_out_2));
  _7_Segment_Display u_7_segment_display_3 (
    .g(letter_3_out_5), .f(letter_3_out_4), .a(letter_3_out_3), .b(letter_3_out_2), .e(letter_3_out_8),
    .d(letter_3_out_7), .c(letter_3_out_6));  // open: dp
  Letter letter_3 (
    .Number(s2_2), .out_8(letter_3_out_8), .out_7(letter_3_out_7), .out_6(letter_3_out_6),
    .out_5(letter_3_out_5), .out_4(letter_3_out_4), .out_3(letter_3_out_3), .out_2(letter_3_out_2));

  // Other names for the same wires on the sheet: s3[6:0] = s2_2

  // Notes on the sheet:
  //   Add
  //   Sub
  //   And
  //   or
  //   Mult
  //   Beq
  //   jum
  //   load
  //   store
  //   addi
endmodule

module Letter (
  input  [6:0] Number,
  output out_2,
  output out_3,
  output out_4,
  output out_5,
  output out_6,
  output out_7,
  output out_8
);


  assign out_2 = Number[0];
  assign out_3 = Number[1];
  assign out_4 = Number[2];
  assign out_5 = Number[3];
  assign out_6 = Number[4];
  assign out_7 = Number[5];
  assign out_8 = Number[6];
endmodule

module OpChooser (
  input  add,
  input  sub,
  input  \and ,
  input  \or ,
  input  mult,
  input  beq,
  input  jump,
  input  load,
  input  store,
  input  addi,
  output s3,
  output s2,
  output s1,
  output s0
);

  or or_1 (s3, addi, store, load);
  or or_2 (s2, jump, beq, mult, \or );
  or or_3 (s1, addi, jump, beq, \and , sub);
  or or_4 (s0, store, jump, mult, \and , add);
endmodule

module Register (
  input  [4:0] rs,
  input  [31:0] in_rd,
  input  [4:0] rt,
  input  [4:0] rd,
  output [31:0] output_rs,
  output [31:0] output_rt
);

  wire Clock;
  wire [31:0] demultiplexer_1_out2, demultiplexer_1_out4, demultiplexer_1_out6, demultiplexer_1_out8, i1, i2,
       i3, i4, i5, i6, i7, i8, i9, i10, i11, i12, i13, i14, i15, i16, i17, i18, i19, i20, i21, i22, i23, i24,
       i25, i26, i27, i28, i29, i30, i31, i32, o1, o2, o3, o4, o5, o6, o7, o8, o9, o10, o11, o12, o13, o14,
       o15, o16, o17, o18, o19, o20, o21, o22, o23, o24, o25, o26, o27, o28, o29, o30, o31, o32;

  Multiplexer #(.select(5), .width(32), .enable("false")) multiplexer_1 (
    .in0(o1), .in1(o2), .in2(o3), .in3(o4), .in4(o5), .in5(o6), .in6(o7), .in7(o8), .in8(o9), .in9(o10),
    .in10(o11), .in11(o12), .in12(o13), .in13(o14), .in14(o15), .in15(o16), .in16(o17), .in17(o18),
    .in18(o19), .in19(o20), .in20(o21), .in21(o22), .in22(o23), .in23(o24), .in24(o25), .in25(o26),
    .in26(o27), .in27(o28), .in28(o29), .in29(o30), .in30(o31), .in31(o32), .out(output_rs), .sel(rs));
  Multiplexer #(.select(5), .width(32), .enable("false")) multiplexer_2 (
    .in0(o1), .in1(o2), .in2(o3), .in3(o4), .in4(o5), .in5(o6), .in6(o7), .in7(o8), .in8(o9), .in9(o10),
    .in10(o11), .in11(o12), .in12(o13), .in13(o14), .in14(o15), .in15(o16), .in16(o17), .in17(o18),
    .in18(o19), .in19(o20), .in20(o21), .in21(o22), .in22(o23), .in23(o24), .in24(o25), .in25(o26),
    .in26(o27), .in27(o28), .in28(o29), .in29(o30), .in30(o31), .in31(o32), .out(output_rt), .sel(rt));
  Clock clock_1 (.out(Clock));
  Demultiplexer #(.select(5), .width(32), .enable("false")) demultiplexer_1 (
    .out0(i1), .out1(i2), .out2(demultiplexer_1_out2), .out3(i4), .out4(demultiplexer_1_out4), .out5(i6),
    .out6(demultiplexer_1_out6), .out7(i8), .out8(demultiplexer_1_out8), .out9(i10), .out10(i11),
    .out11(i12), .out12(i13), .out13(i14), .out14(i15), .out15(i16), .out16(i17), .out17(i18), .out18(i19),
    .out19(i20), .out20(i21), .out21(i22), .out22(i23), .out23(i24), .out24(i25), .out25(i26), .out26(i27),
    .out27(i28), .out28(i29), .out29(i30), .out30(i31), .out31(i32), .in(in_rd), .sel(rd));
  Register_part #(.width(32)) register_1 (.D(i1), .Q(o1), .clk(Clock));  // open: en, clr
  Register_part #(.width(32)) register_2 (.D(i9), .Q(o9), .clk(Clock));  // open: en, clr
  Register_part #(.width(32)) register_3 (.D(i17), .Q(o17), .clk(Clock));  // open: en, clr
  Register_part #(.width(32)) register_4 (.D(i25), .Q(o25), .clk(Clock));  // open: en, clr
  Register_part #(.width(32)) register_5 (.D(i2), .Q(o2), .clk(Clock));  // open: en, clr
  Register_part #(.width(32)) register_6 (.D(i10), .Q(o10), .clk(Clock));  // open: en, clr
  Register_part #(.width(32)) register_7 (.D(i18), .Q(o18), .clk(Clock));  // open: en, clr
  Register_part #(.width(32)) register_8 (.D(i26), .Q(o26), .clk(Clock));  // open: en, clr
  Register_part #(.width(32)) register_9 (.D(i3), .Q(o3), .clk(Clock));  // open: en, clr
  Register_part #(.width(32)) register_10 (.D(i11), .Q(o11), .clk(Clock));  // open: en, clr
  Register_part #(.width(32)) register_11 (.D(i19), .Q(o19), .clk(Clock));  // open: en, clr
  Register_part #(.width(32)) register_12 (.D(i27), .Q(o27), .clk(Clock));  // open: en, clr
  Register_part #(.width(32)) register_13 (.D(i4), .Q(o4), .clk(Clock));  // open: en, clr
  Register_part #(.width(32)) register_14 (.D(i12), .Q(o12), .clk(Clock));  // open: en, clr
  Register_part #(.width(32)) register_15 (.D(i20), .Q(o20), .clk(Clock));  // open: en, clr
  Register_part #(.width(32)) register_16 (.D(i28), .Q(o28), .clk(Clock));  // open: en, clr
  Register_part #(.width(32)) register_17 (.D(i5), .Q(o5), .clk(Clock));  // open: en, clr
  Register_part #(.width(32)) register_18 (.D(i13), .Q(o13), .clk(Clock));  // open: en, clr
  Register_part #(.width(32)) register_19 (.D(i21), .Q(o21), .clk(Clock));  // open: en, clr
  Register_part #(.width(32)) register_20 (.D(i29), .Q(o29), .clk(Clock));  // open: en, clr
  Register_part #(.width(32)) register_21 (.D(i6), .Q(o6), .clk(Clock));  // open: en, clr
  Register_part #(.width(32)) register_22 (.D(i14), .Q(o14), .clk(Clock));  // open: en, clr
  Register_part #(.width(32)) register_23 (.D(i22), .Q(o22), .clk(Clock));  // open: en, clr
  Register_part #(.width(32)) register_24 (.D(i30), .Q(o30), .clk(Clock));  // open: en, clr
  Register_part #(.width(32)) register_25 (.D(i7), .Q(o7), .clk(Clock));  // open: en, clr
  Register_part #(.width(32)) register_26 (.D(i15), .Q(o15), .clk(Clock));  // open: en, clr
  Register_part #(.width(32)) register_27 (.D(i23), .Q(o23), .clk(Clock));  // open: en, clr
  Register_part #(.width(32)) register_28 (.D(i31), .Q(o31), .clk(Clock));  // open: en, clr
  Register_part #(.width(32)) register_29 (.D(i8), .Q(o8), .clk(Clock));  // open: en, clr
  Register_part #(.width(32)) register_30 (.D(i16), .Q(o16), .clk(Clock));  // open: en, clr
  Register_part #(.width(32)) register_31 (.D(i24), .Q(o24), .clk(Clock));  // open: en, clr
  Register_part #(.width(32)) register_32 (.D(i32), .Q(o32), .clk(Clock));  // open: en, clr
endmodule
